# Fritzing sketch Fritzing_sketch (saved by Fritzing 0.9.3b)

parts:
  Raspberry_Pi_1 = Raspberry Pi 3 [part_number=RPI-3-V1.2]
  S1 = H-Bridge with L298N
  18650_holder1 = 18650 holder [package="DIP (Dual Inline) [THT]"]
  18650_holder2 = 18650 holder [package="DIP (Dual Inline) [THT]"]
  M1 = DC Motor
  M2 = DC Motor

nets:
  N1: Raspberry_Pi_1.GIPO17, S1.IN1
  N2: Raspberry_Pi_1.GIPO22, S1.IN2
  N3: Raspberry_Pi_1.GIPO24, S1.IN4
  N4: Raspberry_Pi_1.GIPO23, S1.IN3
  GND: Raspberry_Pi_1.GND, S1.GND, 18650_holder2.holder_-
  N5: S1.5V, 18650_holder1.holder_+
  N6: S1.ENA, S1.ENA-5V
  N7: S1.ENB, S1.ENB-5V
  N8: S1.M1-01, M1.pin_2
  N9: S1.M1-02, M1.pin_1
  N10: S1.M2-01, M2.pin_2
  N11: S1.M2-02, M2.pin_1
  N12: 18650_holder1.holder_-, 18650_holder2.holder_+

custom parts:
  H-Bridge with L298N: h-bridge
  18650 holder: Акум формата 18650 в холдере
